# Fritzing sketch DesbloqueandoPortas (saved by Fritzing 0.9.3b)

parts:
  LCM1602_IIC1 = LCM1602 IIC [part_number="LCM1602 IIC" chip_label="LCM1602 IIC" package="DIP (Dual Inline) [THT]"]
  LCD1 = LCD screen
  Matrix_keypad1 = KEYPAD 4x4
  Componente1 = Arduino Uno (Rev3) - ICSP
  KY-1 = Keyes Relay [package=THT]

nets:
  VSS: LCM1602_IIC1.VSS, LCD1.VSS
  VDD: LCM1602_IIC1.VDD, LCD1.VDD
  N1: LCM1602_IIC1.V0, LCD1.V0
  N2: LCM1602_IIC1.RS, LCD1.RS
  N3: LCM1602_IIC1.RW, LCD1.R/W
  N4: LCM1602_IIC1.E, LCD1.E
  N5: LCM1602_IIC1.D0, LCD1.DB0
  N6: LCM1602_IIC1.D1, LCD1.DB1
  N7: LCM1602_IIC1.D2, LCD1.DB2
  N8: LCM1602_IIC1.D3, LCD1.DB3
  N9: LCM1602_IIC1.D4, LCD1.DB4
  N10: LCM1602_IIC1.D5, LCD1.DB5
  N11: LCM1602_IIC1.D6, LCD1.DB6
  N12: LCM1602_IIC1.D7, LCD1.DB7
  N13: LCM1602_IIC1.A, LCD1.LED+
  N14: LCM1602_IIC1.K, LCD1.LED-
  GND: LCM1602_IIC1.GND, Componente1.GND, KY-1.ground
  VCC: LCM1602_IIC1.VCC, Componente1.5V, KY-1.signal
  N15: LCM1602_IIC1.SDA, Componente1.A4/SDA
  N16: LCM1602_IIC1.SCL, Componente1.A5/SCL
  N17: LCM1602_IIC1.LED_A, LCM1602_IIC1.LED_B
  N18: Matrix_keypad1.col1, Componente1.D9_PWM
  N19: Matrix_keypad1.col2, Componente1.D8
  N20: Matrix_keypad1.col3, Componente1.D7
  N21: Matrix_keypad1.col4, Componente1.D6_PWM
  N22: Matrix_keypad1.row1, Componente1.D5_PWM
  N23: Matrix_keypad1.row2, Componente1.D4
  N24: Matrix_keypad1.row3, Componente1.D3_PWM
  N25: Matrix_keypad1.row4, Componente1.D2
  N26: Componente1.D11_PWM/MOSI, KY-1.power

custom parts:
  LCM1602 IIC: I2C-Module to use a 1602 or 2004 LCD on with the wire.h libory Serial LCD Modul
  KEYPAD 4x4: Matrix keypad 16 buttons, 4 rows x 4 columns
  Keyes Relay: The Keyes 5V relay module is suitable for SCM development, home appliance control. It uses a 5V~12V TIL control signal which can control DC / AC signal.

// code stored in the sketch: DesbloqueandoPorta.ino
#####################################################################################
#  	Arquivo:            DesbloqueandoPorta.ino				                           																								#                                
#       Micro-processador:  Arduino UNO     																																		#
# 		Modulos: i2c, lcd 16x2, relay                                       																												#
#  	Linguagem:	    Wiring / C                                              																												#
#						                                   																																			#
#		Objetivo:  abrir uma porta com senha usando arduino                     																								#
#									            																																					#	  
#		Funcionamento:	 Quando o funcionario chegar na portaria, utilizando a senha        																		#
#                             		ele pode acessar a empresa 																															#
#                           						                                      																												#
#                                                                                   																														#
#                                                                                  																														#
#			                                                            																																	#
#                                      																																								#
#					                                          																																		#
#####################################################################################

// bibliotedas 

//biblioteca i2c
#include <Wire.h> 
// biblioteca da lcd 4X4
#include <LiquidCrystal_I2C.h>
// biblioteca keypad 4x4
#include <Keypad.h>

// set as linhas e as colunas
const byte LINHAS = 4;
const byte COLUNAS = 4;

int contador = 0;
char senha[] = {'1','7','2','8','3','9','\0'};
char palavra[] = {'0','0','0','0','0','0','\0'};

int fechadura = 11;

// matrix numerica 4X4
char matriz[LINHAS][COLUNAS] = 
{
  {'1','2','3','A'},
  {'4','5','6','B'},
  {'7','8','9','C'},
  {'*','0','#','D'},
};

//define os pinos da linha
byte PinosLinhas[LINHAS] = {9,8,7,6};
//define os pinos das colunas
byte PinosColunas[COLUNAS] = {5,4,3,2}; 

// pinos de inicialização do display
LiquidCrystal_I2C lcd(0x27,2,1,0,4,5,6,7,3, POSITIVE);
//LiquidCrystal lcd(0, 1, 2, 3, 4, 5);


//inicializando o teclado 
Keypad kpd = Keypad(makeKeymap(matriz), PinosLinhas, PinosColunas, LINHAS,COLUNAS);


void setup() {
  digitalWrite(fechadura,LOW);
  lcd.begin(16,2);
  lcd.clear();
  lcd.print("DEV crisciano");
  delay(2000);
  lcd.clear();
  lcd.print("Inicializando...");
  delay(2000);
  lcd.clear();
  lcd.print("Digite a senha: ");
  //delay(1000);
  //off_lcd();
  //delay(1000);
  //lcd.setBacklight(LOW);
}

void loop() {
  char key = kpd.getKey();

  if(key)
  {
    lcd.setCursor(0,0);
    lcd.print("Digite a senha: ");
    //delay(1000);
    //off_lcd();
    lcd.setCursor(contador, 1);
    lcd.print("*");
    //on_lcd();
    delay(500);
    palavra[contador] = key;
    contador++;
    if(contador == 6){
      palavra[contador] = '\0';
      if((palavra[0] == senha[0]) && (palavra[1] == senha[1]) && (palavra[3] == senha[3]) && (palavra[4] == senha[4]) && (palavra[5] == senha[5]) && (palavra[6] == senha[6])){
        lcd.clear();
        lcd.print("Senha correta!");
        delay(2000);
        contador = 0;
        lcd.clear();
        lcd.print("Digite a senha: ");
        digitalWrite(fechadura , HIGH);
        delay(1500);
        digitalWrite(fechadura, LOW); 
        }else{
          lcd.clear();
          lcd.print("Senha incorreta!");
          delay(2000);
          contador = 0;
          lcd.clear();
          lcd.print("Digite a senha: ");
          digitalWrite(fechadura, LOW);           
          }
      }
    }
}

void off_lcd(){
  delay(1000);
  lcd.setBacklight(LOW);
}
void on_lcd(){
  //delay(1000);
  lcd.setBacklight(HIGH);
  delay(5000);
  lcd.setBacklight(LOW);
}
